// Logisim project dPCirc.circ as structural Verilog: 17 circuits, main circuit x0
module x0 (
  input  in_1,
  input  in_2,
  output out_3
);

  nor nor_1 (out_3, in_1, in_2);
endmodule

module xa (
  input  in_1,
  input  in_2,
  output out_3
);

  wire n0y_1_out_3;

  _0Y u_0y_1 (.in_1(in_1), .in_2(in_2), .out_3(n0y_1_out_3));
  not not_1 (out_3, n0y_1_out_3);
endmodule

module xb (
  input  in_1,
  input  in_2,
  output out_3
);

  wire not_1_out;

  not not_1 (not_1_out, in_1);
  and and_1 (out_3, not_1_out, in_2);
endmodule

module xc (
  input  in_1,
  input  in_2,
  output out_3
);

  xor xor_1 (out_3, in_1, in_2);
endmodule

module _0a (
  input  in_1,
  input  in_2,
  output out_3
);

  wire b2_1_out_3;

  b2 b2_1 (.in_1(in_1), .in_2(in_2), .out_3(b2_1_out_3));
  not not_1 (out_3, b2_1_out_3);
endmodule

module _0b (
  input  in_1,
  input  in_2,
  output out_3
);

  wire a2_1_out_3;

  a2 a2_1 (.in_1(in_1), .in_2(in_2), .out_3(a2_1_out_3));
  not not_1 (out_3, a2_1_out_3);
endmodule

module _0c (
  input  in_1,
  input  in_2,
  output out_3
);

  nand nand_1 (out_3, in_1, in_2);
endmodule

module x2 (
  input  in_1,
  input  in_2,
  output out_3
);

  and and_1 (out_3, in_1, in_2);
endmodule

module _02 (
  input  in_1,
  input  in_2,
  output out_3
);

  xnor xnor_1 (out_3, in_1, in_2);
endmodule

module a2 (
  input  in_1,
  input  in_2,
  output out_3
);

  wire and_1_out, xa_1_out_3;

  xa xa_1 (.in_1(in_1), .in_2(in_2), .out_3(xa_1_out_3));
  and and_1 (and_1_out, in_1, in_2);
  or or_1 (out_3, xa_1_out_3, and_1_out);
endmodule

module b2 (
  input  in_1,
  input  in_2,
  output out_3
);

  wire and_1_out, xb_1_out_3;

  xb xb_1 (.in_1(in_1), .in_2(in_2), .out_3(xb_1_out_3));
  and and_1 (and_1_out, in_1, in_2);
  or or_1 (out_3, xb_1_out_3, and_1_out);
endmodule

module c2 (
  input  in_1,
  input  in_2,
  output out_3
);

  or or_1 (out_3, in_1, in_2);
endmodule

module _0X (
  input  in_1,
  input  in_2,
  output out_3
);

  wire xb_1_out_3;

  xb xb_1 (.in_1(in_1), .in_2(in_2), .out_3(xb_1_out_3));
  not not_1 (out_3, xb_1_out_3);
endmodule

module _0Y (
  input  in_1,
  input  in_2,
  output out_3
);

  wire and_1_out, b2_1_out_3, not_1_out, not_2_out;

  not not_1 (not_1_out, in_1);
  not not_2 (not_2_out, in_2);
  and and_1 (and_1_out, not_1_out, not_2_out);
  b2 b2_1 (.in_1(in_1), .in_2(in_2), .out_3(b2_1_out_3));
  or or_1 (out_3, and_1_out, b2_1_out_3);
endmodule

module _0Z (
  input  in_1,
  input  in_2,
  output out_3
);

  wire not_1_out, or_1_out, or_2_out;

  not not_1 (not_1_out, in_1);
  or or_1 (or_1_out, not_1_out, in_2);
  or or_2 (or_2_out, in_1, in_2);
  or or_3 (or_2_out, in_1, in_2);
  or or_4 (out_3, or_1_out, or_2_out);
endmodule

module nl (
  input  in_1,
  input  in_2,
  output out_3
);

  wire n0z_1_out_3;

  _0Z u_0z_1 (.in_1(in_1), .in_2(in_2), .out_3(n0z_1_out_3));
  not not_1 (out_3, n0z_1_out_3);
endmodule

module test (
  input  in_1,
  input  in_2
);

  wire a2_1_out_3, b2_1_out_3, c2_1_out_3, n0a_1_out_3, n0b_1_out_3, n0c_1_out_3, n0x_1_out_3, n0y_1_out_3,
       n0z_1_out_3, n02_1_out_3, nl_1_out_3, x0_1_out_3, x2_1_out_3, xa_1_out_3, xb_1_out_3, xc_1_out_3;

  LED led_1 (.in(x0_1_out_3));
  x0 x0_1 (.in_1(in_1), .in_2(in_2), .out_3(x0_1_out_3));
  LED led_2 (.in(xa_1_out_3));
  LED led_3 (.in(xb_1_out_3));
  xb xb_1 (.in_1(in_1), .in_2(in_2), .out_3(xb_1_out_3));
  xa xa_1 (.in_1(in_1), .in_2(in_2), .out_3(xa_1_out_3));
  LED led_4 (.in(xc_1_out_3));
  LED led_5 (.in(xc_1_out_3));
  xc xc_1 (.in_1(in_1), .in_2(in_2), .out_3(xc_1_out_3));
  LED led_6 (.in(n0a_1_out_3));
  LED led_7 (.in(n0b_1_out_3));
  _0a u_0a_1 (.in_1(in_1), .in_2(in_2), .out_3(n0a_1_out_3));
  _0b u_0b_1 (.in_1(in_1), .in_2(in_2), .out_3(n0b_1_out_3));
  LED led_8 (.in(x2_1_out_3));
  LED led_9 (.in(n0c_1_out_3));
  LED led_10 (.in(x2_1_out_3));
  x2 x2_1 (.in_1(in_1), .in_2(in_2), .out_3(x2_1_out_3));
  _0c u_0c_1 (.in_1(in_1), .in_2(in_2), .out_3(n0c_1_out_3));
  LED led_11 (.in(a2_1_out_3));
  LED led_12 (.in(n02_1_out_3));
  _02 u_02_1 (.in_1(in_1), .in_2(in_2), .out_3(n02_1_out_3));
  a2 a2_1 (.in_1(in_1), .in_2(in_2), .out_3(a2_1_out_3));
  LED led_13 (.in(c2_1_out_3));
  LED led_14 (.in(b2_1_out_3));
  LED led_15 (.in(c2_1_out_3));
  b2 b2_1 (.in_1(in_1), .in_2(in_2), .out_3(b2_1_out_3));
  c2 c2_1 (.in_1(in_1), .in_2(in_2), .out_3(c2_1_out_3));
  LED led_16 (.in(n0x_1_out_3));
  _0X u_0x_1 (.in_1(in_1), .in_2(in_2), .out_3(n0x_1_out_3));
  LED led_17 (.in(n0z_1_out_3));
  LED led_18 (.in(n0y_1_out_3));
  _0Z u_0z_1 (.in_1(in_1), .in_2(in_2), .out_3(n0z_1_out_3));
  _0Y u_0y_1 (.in_1(in_1), .in_2(in_2), .out_3(n0y_1_out_3));
  LED led_19 (.in(nl_1_out_3));
  LED led_20 (.in(nl_1_out_3));
  nl nl_1 (.in_1(in_1), .in_2(in_2), .out_3(nl_1_out_3));
endmodule
