// Logisim project mPCirc.circ as structural Verilog: 5 circuits, main circuit e
module e (
  input  in_1,
  output out_2
);

  not not_1 (out_2, in_1);
endmodule

module b (
  input  in_1,
  output out_2
);

  buf buffer_1 (out_2, in_1);
endmodule

module i (
  input  in_1,
  output out_2
);

  wire not_1_out;

  not not_1 (not_1_out, in_1);
  or or_1 (out_2, not_1_out, in_1);
endmodule

module l (
  input  in_1,
  output out_2
);

  wire i_1_out_2;

  i i_1 (.in_1(in_1), .out_2(i_1_out_2));
  not not_1 (out_2, i_1_out_2);
endmodule

module test (
  input  in_1
);

  wire b_1_out_2, e_1_out_2, i_1_out_2, l_1_out_2;

  LED led_1 (.in(e_1_out_2));
  e e_1 (.in_1(in_1), .out_2(e_1_out_2));
  LED led_2 (.in(b_1_out_2));
  LED led_3 (.in(i_1_out_2));
  i i_1 (.in_1(in_1), .out_2(i_1_out_2));
  b b_1 (.in_1(in_1), .out_2(b_1_out_2));
  LED led_4 (.in(l_1_out_2));
  l l_1 (.in_1(in_1), .out_2(l_1_out_2));
endmodule
